# Fritzing sketch OTTORoughSketch (saved by Fritzing 0.9.2b)

parts:
  FubarinoSD1 = Fubarino SD [chip_label=FubarinoSD package="DIP (Dual Inline) [THT]"]
  M1 = DC Motor
  M2 = DC Motor
  Part1 = 9 Degrees of Freedom - Sensor Stick
  U1 = RELAY [package=relay-jzc]  # not connected

nets:
  N1: FubarinoSD1.Digital0, Part1.SDA
  N2: FubarinoSD1.Digital1, Part1.SCL
  N3: FubarinoSD1.Digital2, M2.pin_2
  N4: FubarinoSD1.Digital3, M2.pin_1
  N5: FubarinoSD1.Digital4, M1.pin_2
  N6: FubarinoSD1.Digital7, M1.pin_1

custom parts:
  Fubarino SD: Fubarino SD, v1.5, a chipKIT board.
